// Logisim project Lab7JessicaNoel.circ as structural Verilog: 3 circuits, main circuit ParityGenerator
module XOR (
  input  X,
  input  Y,
  input  X_2,
  input  Y_2,
  input  in_5,
  input  in_6,
  output out_7,
  output out_8,
  output out_9
);

  wire and_1_out, and_3_out, and_4_out, and_5_out, not_1_out, not_2_out, not_3_out, not_4_out, or_1_out,
       or_3_out;

  not not_1 (not_1_out, X_2);
  and and_1 (and_1_out, Y, X);
  not not_2 (not_2_out, and_1_out);
  or or_1 (or_1_out, Y, X);
  not not_3 (not_3_out, Y_2);
  and and_2 (out_7, not_2_out, or_1_out);
  and and_3 (and_3_out, not_3_out, X_2);
  and and_4 (and_4_out, Y_2, not_1_out);
  or or_2 (out_8, and_3_out, and_4_out);
  and and_5 (and_5_out, in_6, in_5);
  or or_3 (or_3_out, in_6, in_5);
  not not_4 (not_4_out, and_5_out);
  and and_6 (out_9, not_4_out, or_3_out);

  // Notes on the sheet:
  //   x XOR y = (x or y) and not (x and y)
  //   Minterm Expansion
  //   Both circuits are equivalent and valid representations of x XOR y
endmodule

module MyXOR (
  input  in_1,
  input  in_2,
  input  in_3,
  input  in_4,
  output out_5,
  output out_6
);

  wire and_1_out, and_2_out, and_3_out, not_1_out, not_2_out, not_3_out, or_1_out;

  not not_1 (not_1_out, in_3);
  not not_2 (not_2_out, in_4);
  and and_1 (and_1_out, in_2, in_1);
  or or_1 (or_1_out, in_1, in_2);
  and and_2 (and_2_out, not_1_out, in_4);
  and and_3 (and_3_out, in_3, not_2_out);
  not not_3 (not_3_out, and_1_out);
  and and_4 (out_5, not_3_out, or_1_out);
  or or_2 (out_6, and_2_out, and_3_out);

  // Notes on the sheet:
  //   Practice using Logism by recreating one of the implementations from XOR!
endmodule

module ParityGenerator (
  input  x,
  input  y,
  input  z,
  output out_4
);

  wire and_1_out, and_2_out, not_1_out, not_2_out, or_1_out, or_2_out, or_4_out;

  and and_1 (and_1_out, x, y);
  and and_2 (and_2_out, z, and_1_out);
  not not_1 (not_1_out, y);
  or or_1 (or_1_out, and_2_out, and_1_out, or_2_out);
  buf or_2 (or_2_out, not_1_out);  // OR_Gate
  not not_2 (not_2_out, or_1_out);
  or or_3 (out_4, and_2_out, or_4_out);
  buf or_4 (or_4_out, not_2_out);  // OR_Gate

  // Notes on the sheet:
  //   inputs
  //   output
  //   Write your parity circuit here
  //   the output = 1 if an odd number of inputs (1 or 3) are 1, otherwise 0
  //   ONLY use: NOT, AND, OR, and any custom functions you write (included in the .circ submission)
  //   Jessica Noel 'I pledge my honor that I have abided by the Stevens Honor System'
endmodule
