// Logisim project Lab8.circ as structural Verilog: 4 circuits, main circuit D_Latch
module NOR (
  input  X,
  input  Y,
  output Out
);

  wire or_1_out;

  or or_1 (or_1_out, X, Y);
  not not_1 (Out, or_1_out);

  // Notes on the sheet:
  //   NOR
  //   Using only OR and NOT gates, please create the NOR gate
  //   This gate returns 1 if both bits are 0, and 1 otherwise
  //   light green=1
  //   dark green=0
endmodule

module TwoBit_Decoder (
  input  in_1,
  input  in_2,
  output out_3,
  output out_4,
  output out_5,
  output out_6
);

  wire not_1_out, not_2_out, not_3_out, not_4_out;

  not not_1 (not_1_out, in_1);
  not not_2 (not_2_out, in_2);
  not not_3 (not_3_out, in_1);
  not not_4 (not_4_out, in_2);
  and and_1 (out_3, not_2_out, not_3_out);
  and and_2 (out_4, in_2, not_1_out);
  and and_3 (out_5, not_4_out, in_1);
  and and_4 (out_6, in_2, in_1);

  // Notes on the sheet:
  //   2 Bit Decoder
  //   00 should turn on Output0 and nothing else
  //   01 should turn on Output1 and nothing else
  //   10 should turn on Output2 and nothing else
  //   11 should turn on Output3 and nothing else
  //   Using only AND and NOT gates, please write this decoder circuit
  //   Consider the input 01 to mean Input0 is 0, Input1 is 1.
endmodule

module SR_Latch (
  input  S,
  input  R,
  output Q
);

  wire not_1_out, or_1_out, or_2_out;

  or or_1 (or_1_out, S, Q);
  or or_2 (or_2_out, not_1_out, R);
  not not_1 (not_1_out, or_1_out);
  not not_2 (Q, or_2_out);

  // Notes on the sheet:
  //   R: pull=down
  //   Q: pull=up
  //   S: pull=down
  //   S-R Latch
  //   Using two of the NOR gate you just wrote, create an S-R latch
  //   The behavior of this circuit is not defined if both S and R are on
  //   Notice that in the SR=00 state, the output Q could be either 0 or 1 !  
  //   Logism will also throw this error every time you open a successfully built latch's .circ file
  //   In this circuit, each input feeds one NOR gate, and the output of each NOR gate loops intp the other input's gate
  //   This makes the latch different from any circuit you've worked with before, and the basis for computer memory.
  //   If your wires turn red and Logism yells at you for apparent oscillation, you've messed something up.
  //   Then, draw your loop back in and it should function properly. If not, go to someone's office hours.
  //   The output should become 1 when S is turned on, 0 when R is turned on, and remain whatever it is if both are turned off
  //   To fix this, break any loop in your circuit, then in the Simulate menu up top turn "Simulation Enabled" on and off again
endmodule

module D_Latch (
  input  D,
  input  strobe,
  output out_3
);

  wire and_1_out, and_2_out, not_1_out, not_2_out, or_1_out, or_2_out;

  not not_1 (not_1_out, D);
  and and_1 (and_1_out, D, strobe);
  and and_2 (and_2_out, not_1_out, strobe);
  or or_1 (or_1_out, and_1_out, out_3);
  not not_2 (not_2_out, or_1_out);
  not not_3 (out_3, or_2_out);
  or or_2 (or_2_out, not_2_out, and_2_out);

  // Notes on the sheet:
  //   D Latch
  //   Jessica Noel
  //   I pledge my honor that I have abided by the Stevens Honor System.
  //   Your circuit should use 2 NOR gates, 2 AND gates, and 1 NOT. 
  //   If Strobe is 1, then the value of output should become the value of D
  //   This avoids the situation where both S and R are on
  //   The whole oscillation deal also applies here - be ready to fight Logism
  //   The D latch improves on the S-R by having one input, D, and a Strobe.
  //   If Strobe is 0, then the value of D should have no impact at all on the output bit
  //   If Strobe is 0, you need to stop any inputs to your S-R latch, consider how to do that
  //   D will feed eventually into both S and R inputs to the S-R latch, just invert one of them
  //   The S-R latch we just designed has several flaws, such as both S and R being 1 not having defined output
  //   This is accomplished with an S-R latch as part of the D latch - do not drag in your pre-built SR latch, create it anew!
  //   Hint: Check out week8.pdf
endmodule
